// Logisim project Caculation.circ as structural Verilog: 1 circuit, main circuit main
module main (
  input  [12:0] year_in,
  output [12:0] out_2,
  output [2:0] out_3,
  output [1:0] out_4
);

  Comparator #(.width(13)) comparator_1 (.a(year_in), .b({13{1'b0}}), .lt(out_4[0]));  // open: gt, eq
  Subtractor #(.width(13)) subtractor_1 (.a(year_in), .b(13'h7e3), .out(out_2));  // open: bin, bout
  Comparator #(.width(13)) comparator_2 (.a(year_in), .b(13'h7e3), .gt(out_3[2]), .eq(out_3[1]), .lt(out_3[0]));
  or or_1 (out_4[1], out_3[0], out_3[2]);

  // Notes on the sheet:
  //   Check if <0
  //   2019 in hex
  //   Check if travel forward/backward
  //   001: Back in time
  //   100: To the future
  //   010: Stay at 2019
endmodule
