// Logisim project Destination.circ as structural Verilog: 1 circuit, main circuit main
module main (
  input  Temperature,
  input  Radiation,
  input  Oxygen,
  input  Life,
  input  [8:0] in_5,
  input  [8:0] in_6,
  input  [8:0] in_7,
  input  in_8,
  output [1:0] out_9,
  output [8:0] out_10
);

  wire and_1_out, and_2_out, and_3_out, comparator_1_eq, comparator_1_lt, comparator_2_lt, not_1_out,
       or_1_out;
  wire [0:0] comparator_1_gt;

  Comparator #(.width(9), .mode("unsigned")) comparator_1 (
    .a(in_5), .b(in_6), .gt(comparator_1_gt[0]), .eq(comparator_1_eq), .lt(comparator_1_lt));
  or or_1 (or_1_out, comparator_1_eq, comparator_1_lt);
  not not_1 (not_1_out, Radiation);
  and and_1 (and_1_out, Temperature, not_1_out);
  and and_2 (and_2_out, Oxygen, Life);
  Shifter #(.width(9), .shift("lr")) shifter_1 (.in(in_5), .\dist ({{3{in_8}}, comparator_1_gt[0]}), .out(out_10));
  and and_3 (and_3_out, and_1_out, and_2_out);
  Comparator #(.width(9), .mode("unsigned")) comparator_2 (.a(out_10), .b(in_7), .lt(comparator_2_lt));  // open: gt, eq
  or or_2 (out_9[1], comparator_2_lt, or_1_out);
  not not_2 (out_9[0], and_3_out);

  // Notes on the sheet:
  //   Altitude check
  //   Habitability (ERR)
endmodule
